// Logisim project cronometro.circ as structural Verilog: 17 circuits, main circuit Cronometro
module Cronometro (
);

  wire A_1, A_2, A_3, A_4, A_5, A_6, and_2_out, and_3_out, and_4_out, and_5_out, and_6_out, and_7_out,
       and_8_out, and_9_out, B_1, B_2, B_3, B_4, B_5, B_6, C_1, C_2, C_3, C_4, C_5, C_6, CB_1, CB_2, CB_3,
       CB_4, CB_5, CB_6, Clockers, Clockers_out, Cresce, Cresce_Pulse, D_1, D_2, D_3, D_4, D_5, D_6, E_1,
       E_2, E_3, E_4, E_5, E_6, F_1, F_2, F_3, F_4, F_5, F_6, G_1, G_2, G_3, G_4, G_5, G_6, Horas, Liga,
       Liga_Desliga_out, Manual, Manual_Automatico_out, Minutos, my_mux_down_1_saida, my_mux_down_2_saida,
       my_mux_down_3_saida, my_mux_down_4_saida, my_mux_up_1_saida, my_mux_up_2_saida, my_mux_up_3_saida,
       my_mux_up_4_saida, my_mux_up_5_saida, my_mux_up_6_saida, not_1_out, num_02_1_out_5, num_03_1_out_5,
       or_1_out, or_2_out, or_3_out, or_4_out, or_5_out, or_6_out, or_7_out, Q1_1, Q1_2, Q1_3, Q1_4, Q1_5,
       Q1_6, Q2_1, Q2_2, Q2_3, Q2_4, Q2_5, Q2_6, Q3_1, Q3_2, Q3_3, Q3_4, Q3_5, Q3_6, Q4_1, Q4_2, Q4_3, Q4_4,
       Q4_5, Q4_6, Q_CB_1, Q_CB_2, Q_CB_3, Q_CB_4, Q_CB_5, Reset, ResetH, Segundos;
  wire [3:0] Force3;
  wire [3:3] d_ff_6_q;

  Clock u_Clockers (.out(Clockers_out));
  Button Liga_Desliga (.out(Liga_Desliga_out));
  Button Cresce_Descrece (.out(Cresce_Pulse));
  Button Manual_Automatico (.out(Manual_Automatico_out));
  Button u_Reset (.out(Reset));
  Button u_Segundos (.out(Segundos));
  Button u_Minutos (.out(Minutos));
  Button u_Horas (.out(Horas));
  and and_1 (Clockers, Clockers_out, 1'b1);
  Alavanca alavanca_1 (.in_1(Liga_Desliga_out), .out_2(Liga));
  Alavanca alavanca_2 (.in_1(Cresce_Pulse), .out_2(Cresce));
  Alavanca alavanca_3 (.in_1(Manual_Automatico_out), .out_2(Manual));
  _7_Segment_Display #(.decimalPoint("false")) u_7_segment_display_1 (
    .g(G_6), .f(F_6), .a(A_6), .b(B_6), .e(E_6), .d(D_6), .c(C_6));
  _7_Segment_Display #(.decimalPoint("false")) u_7_segment_display_2 (
    .g(G_5), .f(F_5), .a(A_5), .b(B_5), .e(E_5), .d(D_5), .c(C_5));
  _7_Segment_Display #(.decimalPoint("false")) u_7_segment_display_3 (
    .g(G_4), .f(F_4), .a(A_4), .b(B_4), .e(E_4), .d(D_4), .c(C_4));
  _7_Segment_Display #(.decimalPoint("false")) u_7_segment_display_4 (
    .g(G_3), .f(F_3), .a(A_3), .b(B_3), .e(E_3), .d(D_3), .c(C_3));
  _7_Segment_Display #(.decimalPoint("false")) u_7_segment_display_5 (
    .g(G_2), .f(F_2), .a(A_2), .b(B_2), .e(E_2), .d(D_2), .c(C_2));
  CountMOD10 countmod10_1 (
    .Cresce_Descrece(Cresce), .Reset(Reset), .Impulso(Segundos), .Clock(Clockers),
    .Manual_Automatico(Manual), .Liga(Liga), .Carry_Borrow(CB_1), .Q1(Q1_1), .Q2(Q2_1), .Q3(Q3_1), .Q4(Q4_1));  // open: Force_Num
  _7_Segment_Display #(.decimalPoint("false")) u_7_segment_display_6 (
    .g(G_1), .f(F_1), .a(A_1), .b(B_1), .e(E_1), .d(D_1), .c(C_1));
  D_Flip_Flop d_ff_1 (.D(CB_1), .clk(my_mux_up_1_saida), .Q(Q_CB_1), .reset(or_1_out));  // open: Qn, preset
  My_Mux_Up my_mux_up_1 (.Entrada_0(Clockers), .Entrada_1(Segundos), .Select_0(Manual), .Saida(my_mux_up_1_saida));
  or or_1 (or_1_out, Reset, Cresce_Pulse);
  CountMOD6 countmod6_1 (
    .Liga(Liga), .Cresce_Descresce(Cresce), .Reset(Reset), .Impulso(Q_CB_1), .Clock(Q_CB_1),
    .Manual_Automatico(Manual), .Carry_Borrow(CB_2), .Q1(Q1_2), .Q2(Q2_2), .Q3(Q3_2), .Q4(Q4_2));
  Display display_1 (
    .Q1(Q1_6), .Q2(Q2_6), .Q3(Q3_6), .Q4(Q4_6), .B(B_6), .C(C_6), .D(D_6), .E(E_6), .F(F_6), .G(G_6), .A(A_6));
  and and_2 (and_2_out, CB_1, CB_2, CB_3, CB_4, CB_5, CB_6);
  My_Mux_Up my_mux_up_2 (.Entrada_0(Clockers), .Entrada_1(Segundos), .Select_0(Manual), .Saida(my_mux_up_2_saida));
  Display display_2 (
    .Q1(Q1_5), .Q2(Q2_5), .Q3(Q3_5), .Q4(Q4_5), .B(B_5), .C(C_5), .D(D_5), .E(E_5), .F(F_5), .G(G_5), .A(A_5));
  D_Flip_Flop d_ff_2 (.D(and_3_out), .clk(my_mux_up_2_saida), .Q(Q_CB_2), .reset(or_2_out));  // open: Qn, preset
  and and_3 (and_3_out, CB_2, CB_1);
  or or_2 (or_2_out, Reset, Cresce_Pulse);
  Display display_3 (
    .Q1(Q1_4), .Q2(Q2_4), .Q3(Q3_4), .Q4(Q4_4), .B(B_4), .C(C_4), .D(D_4), .E(E_4), .F(F_4), .G(G_4), .A(A_4));
  CountMOD10 countmod10_2 (
    .Cresce_Descrece(Cresce), .Reset(Reset), .Impulso(Minutos), .Clock(Q_CB_2), .Manual_Automatico(Manual),
    .Liga(Liga), .Carry_Borrow(CB_3), .Q1(Q1_3), .Q2(Q2_3), .Q3(Q3_3), .Q4(Q4_3));  // open: Force_Num
  Display display_4 (
    .Q1(Q1_3), .Q2(Q2_3), .Q3(Q3_3), .Q4(Q4_3), .B(B_3), .C(C_3), .D(D_3), .E(E_3), .F(F_3), .G(G_3), .A(A_3));
  and and_4 (and_4_out, CB_1, CB_2, CB_3);
  My_Mux_Down my_mux_down_1 (.Entrada_0(and_4_out), .Entrada_1(CB_3), .Select_0(Manual), .Saida(my_mux_down_1_saida));
  My_Mux_Up my_mux_up_3 (.Entrada_0(Clockers), .Entrada_1(Minutos), .Select_0(Manual), .Saida(my_mux_up_3_saida));
  Display display_5 (
    .Q1(Q1_2), .Q2(Q2_2), .Q3(Q3_2), .Q4(Q4_2), .B(B_2), .C(C_2), .D(D_2), .E(E_2), .F(F_2), .G(G_2), .A(A_2));
  D_Flip_Flop d_ff_3 (
    .D(my_mux_down_1_saida), .clk(my_mux_up_3_saida), .Q(Q_CB_3), .reset(or_3_out));  // open: Qn, preset
  or or_3 (or_3_out, Reset, Cresce_Pulse);
  Display display_6 (
    .Q1(Q1_1), .Q2(Q2_1), .Q3(Q3_1), .Q4(Q4_1), .B(B_1), .C(C_1), .D(D_1), .E(E_1), .F(F_1), .G(G_1), .A(A_1));
  CountMOD6 countmod6_2 (
    .Liga(Liga), .Cresce_Descresce(Cresce), .Reset(Reset), .Impulso(Q_CB_3), .Clock(Q_CB_3),
    .Manual_Automatico(Manual), .Carry_Borrow(CB_4), .Q1(Q1_4), .Q2(Q2_4), .Q3(Q3_4), .Q4(Q4_4));
  and and_5 (and_5_out, CB_1, CB_2, CB_3, CB_4);
  My_Mux_Down my_mux_down_2 (.Entrada_0(and_5_out), .Entrada_1(CB_4), .Select_0(Manual), .Saida(my_mux_down_2_saida));
  My_Mux_Up my_mux_up_4 (.Entrada_0(Clockers), .Entrada_1(Minutos), .Select_0(Manual), .Saida(my_mux_up_4_saida));
  D_Flip_Flop d_ff_4 (
    .D(my_mux_down_2_saida), .clk(my_mux_up_4_saida), .Q(Q_CB_4), .reset(or_4_out));  // open: Qn, preset
  or or_4 (or_4_out, Reset, Cresce_Pulse);
  or or_5 (or_5_out, Reset, ResetH);
  CountMOD10 countmod10_3 (
    .Cresce_Descrece(Cresce), .Reset(or_5_out), .Impulso(Horas), .Clock(Q_CB_4), .Manual_Automatico(Manual),
    .Force_Num(Force3), .Liga(Liga), .Carry_Borrow(CB_5), .Q1(Q1_5), .Q2(Q2_5), .Q3(Q3_5), .Q4(Q4_5));
  and and_6 (and_6_out, CB_1, CB_2, CB_3, CB_4, CB_5);
  My_Mux_Down my_mux_down_3 (.Entrada_0(and_6_out), .Entrada_1(CB_5), .Select_0(Manual), .Saida(my_mux_down_3_saida));
  My_Mux_Up my_mux_up_5 (.Entrada_0(Clockers), .Entrada_1(Horas), .Select_0(Manual), .Saida(my_mux_up_5_saida));
  D_Flip_Flop d_ff_5 (
    .D(my_mux_down_3_saida), .clk(my_mux_up_5_saida), .Q(Q_CB_5), .reset(or_6_out));  // open: Qn, preset
  or or_6 (or_6_out, Reset, Cresce_Pulse);
  or or_7 (or_7_out, Reset, ResetH);
  CountMOD3 countmod3_1 (
    .Liga(Liga), .Cresce_Descresce(Cresce), .Reset(or_7_out), .Impulso(Q_CB_5), .Clock(Q_CB_5),
    .Manual_Automatico(Manual), .Carry_Borrow(CB_6), .Q1(Q1_6), .Q2(Q2_6), .Q3(Q3_6), .Q4(Q4_6));
  and and_7 (and_7_out, CB_1, CB_2, CB_3, CB_4, CB_5);
  My_Mux_Down my_mux_down_4 (
    .Entrada_0(and_7_out), .Entrada_1(and_8_out), .Select_0(Manual), .Saida(my_mux_down_4_saida));
  D_Flip_Flop d_ff_6 (
    .D(my_mux_down_4_saida), .clk(my_mux_up_6_saida), .Q(d_ff_6_q[3]), .reset(and_9_out));  // open: Qn, preset
  My_Mux_Up my_mux_up_6 (.Entrada_0(Clockers), .Entrada_1(Horas), .Select_0(Manual), .Saida(my_mux_up_6_saida));
  and and_8 (and_8_out, Cresce, CB_6, CB_5);
  and and_9 (and_9_out, num_02_1_out_5, num_03_1_out_5);
  Num_02 num_02_1 (.in_1(Q1_6), .in_2(Q2_6), .in_3(Q3_6), .in_4(Q4_6), .out_5(num_02_1_out_5));
  Num_03 num_03_1 (.in_1(Q1_5), .in_2(Q2_5), .in_3(Q3_5), .in_4(Q4_5), .out_5(num_03_1_out_5));
  assign Force3 = {4{d_ff_6_q[3]}} & 4'b0011;  // AND_Gate and_10, 4 bits wide
  not not_1 (not_1_out, Cresce);
  and and_11 (ResetH, Q2_6, Q3_5, not_1_out);

  // Notes on the sheet:
  //   ENTRADAS
  //   GLOSSÁRIO:
  //   - CB = Carry OU Borrow
  //   CRONÔMETRO
  //   :
  //   Segundos Unidade
  //   :
  //   Segundos Dezena
  //   Chegou no Máximo?
  //   HORAS
  //   DISPLAYS
  //   MINUTOS
  //   Minutos Unidade
  //   SEGUNDOS
  //   Minutos Dezena
  //   Horas Unidade
  //   Horas Dezena
  //   24h Decrescente
  //   Se H = 00 => reset pra 23 no PRÓXIMO clock
  //   24h Crescente
  //   Se H = 24 => reset pra 00
endmodule

module Display (
  input  Q1,
  input  Q2,
  input  Q3,
  input  Q4,
  output A,
  output B,
  output C,
  output D,
  output E,
  output F,
  output G
);

  wire and_1_out, and_2_out, and_3_out, and_4_out, and_5_out, and_6_out, and_7_out, and_8_out, and_9_out,
       and_10_out, and_11_out, not_1_out, not_2_out, not_3_out, not_4_out;

  not not_1 (not_1_out, Q1);
  not not_2 (not_2_out, Q2);
  not not_3 (not_3_out, Q3);
  not not_4 (not_4_out, Q4);
  and and_1 (and_1_out, not_1_out, not_2_out, not_3_out, not_4_out);
  and and_2 (and_2_out, Q1, not_2_out, not_3_out, not_4_out);
  and and_3 (and_3_out, not_1_out, Q2, not_3_out, not_4_out);
  and and_4 (and_4_out, Q1, Q2, not_3_out, not_4_out);
  and and_5 (and_5_out, not_1_out, not_2_out, Q3, not_4_out);
  and and_6 (and_6_out, Q1, not_2_out, Q3, not_4_out);
  and and_7 (and_7_out, not_1_out, Q2, Q3, not_4_out);
  and and_8 (and_8_out, Q1, Q2, Q3, not_4_out);
  and and_9 (and_9_out, not_1_out, not_2_out, not_3_out, Q4);
  and and_10 (and_10_out, Q1, not_2_out, not_3_out, Q4);
  and and_11 (and_11_out, not_1_out, Q2, not_3_out, Q4);
  nor nor_1 (A, and_2_out, and_5_out);
  nor nor_2 (B, and_6_out, and_7_out);
  not not_5 (C, and_3_out);
  nor nor_3 (D, and_2_out, and_5_out, and_8_out, and_10_out);
  or or_1 (E, and_1_out, and_3_out, and_7_out, and_9_out, and_11_out);
  nor nor_4 (F, and_2_out, and_3_out, and_4_out, and_8_out);
  nor nor_5 (G, and_1_out, and_2_out, and_8_out, and_11_out);
endmodule

module CountMOD3 (
  input  Cresce_Descresce,
  input  Reset,
  input  Impulso,
  input  Liga,
  input  Clock,
  input  Manual_Automatico,
  output Carry_Borrow,
  output Q1,
  output Q3,
  output Q2,
  output Q4
);

  wire and_1_out, and_2_out, and_3_out, and_4_out, and_5_out, and_6_out, and_7_out, and_8_out, and_9_out,
       and_10_out, and_11_out, D1, D1_pre, D2, D2_pre, D3, D3_pre, D4, D4_pre, Its_0, Its_2,
       my_mux_up_1_saida, not_1_out, not_2_out, not_3_out, not_4_out, not_5_out, not_6_out, not_7_out,
       not_8_out, not_9_out, not_10_out, or_1_out, or_2_out, or_4_out, R1, R2, R3, R4, S1, S2, S3, S4,
       xnor_1_out, xnor_2_out, xnor_3_out, xor_1_out, xor_2_out, xor_3_out;
  wire [3:0] my_mux_4bits_2_saida, my_mux_4bits_4_saida;

  not not_1 (not_1_out, Q1);
  and and_1 (and_1_out, not_1_out, not_2_out);
  not not_2 (not_2_out, Its_2);
  My_Mux_Down my_mux_down_1 (.Entrada_0(and_1_out), .Entrada_1(and_2_out), .Select_0(Cresce_Descresce), .Saida(D1_pre));
  not not_3 (not_3_out, Q1);
  not not_4 (not_4_out, Its_0);
  and and_2 (and_2_out, not_3_out, not_4_out);
  Num_00 num_00_1 (.in_1(Q1), .in_2(Q2), .in_3(Q3), .in_4(Q4), .out_5(Its_0));
  Num_02 num_02_1 (.in_1(Q1), .in_2(Q2), .in_3(Q3), .in_4(Q4), .out_5(Its_2));
  xor xor_1 (xor_1_out, Q1, Q2);
  not not_5 (not_5_out, Its_2);
  and and_3 (and_3_out, xor_1_out, not_5_out);
  My_Mux_Down my_mux_down_2 (.Entrada_0(and_3_out), .Entrada_1(or_1_out), .Select_0(Cresce_Descresce), .Saida(D2_pre));
  xnor xnor_1 (xnor_1_out, Q1, Q2);
  or or_1 (or_1_out, xnor_1_out, Its_0);
  D_Flip_Flop d_ff_1 (.D(D1), .clk(my_mux_up_1_saida), .Q(Q1), .preset(S1), .reset(R1));  // open: Qn
  D_Flip_Flop d_ff_2 (.D(D2), .clk(my_mux_up_1_saida), .Q(Q2), .preset(S2), .reset(R2));  // open: Qn
  and and_4 (and_4_out, Q1, Q2);
  xor xor_2 (xor_2_out, and_4_out, Q3);
  and and_5 (and_5_out, xor_2_out, not_6_out);
  My_Mux_Up my_mux_up_1 (
    .Entrada_0(Clock), .Entrada_1(Impulso), .Select_0(Manual_Automatico), .Saida(my_mux_up_1_saida));
  not not_6 (not_6_out, Its_2);
  D_Flip_Flop d_ff_3 (.D(D3), .clk(my_mux_up_1_saida), .Q(Q3), .preset(S3), .reset(R3));  // open: Qn
  not not_7 (not_7_out, Cresce_Descresce);
  and and_6 (and_6_out, not_7_out, Its_2);
  and and_7 (and_7_out, Cresce_Descresce, Its_0);
  My_Mux_Down my_mux_down_3 (.Entrada_0(and_5_out), .Entrada_1(and_8_out), .Select_0(Cresce_Descresce), .Saida(D3_pre));
  D_Flip_Flop d_ff_4 (.D(D4), .clk(my_mux_up_1_saida), .Q(Q4), .preset(S4), .reset(R4));  // open: Qn
  or or_2 (or_2_out, Q1, Q2);
  xnor xnor_2 (xnor_2_out, or_2_out, Q3);
  not not_8 (not_8_out, Its_0);
  and and_8 (and_8_out, xnor_2_out, not_8_out);
  or or_3 (Carry_Borrow, and_6_out, and_7_out);
  and and_9 (and_9_out, Q1, Q2, Q3);
  xor xor_3 (xor_3_out, and_9_out, Q4);
  not not_9 (not_9_out, Its_2);
  and and_10 (and_10_out, xor_3_out, not_9_out);
  My_Mux_Down my_mux_down_4 (.Entrada_0(Q1), .Entrada_1(D1_pre), .Select_0(Liga), .Saida(D1));
  My_Mux_4bits my_mux_4bits_1 (
    .Entrada_0(4'b0000), .Entrada_1(my_mux_4bits_2_saida), .Select_0(Reset), .Saida({S4, S3, S2, S1}));
  My_Mux_4bits my_mux_4bits_2 (
    .Entrada_0(4'b0000), .Entrada_1(4'b0010), .Select_0(Cresce_Descresce), .Saida(my_mux_4bits_2_saida));
  My_Mux_Down my_mux_down_5 (
    .Entrada_0(and_10_out), .Entrada_1(and_11_out), .Select_0(Cresce_Descresce), .Saida(D4_pre));
  or or_4 (or_4_out, Q1, Q2, Q3);
  xnor xnor_3 (xnor_3_out, or_4_out, Q4);
  not not_10 (not_10_out, Its_0);
  and and_11 (and_11_out, xnor_3_out, not_10_out);
  My_Mux_Down my_mux_down_6 (.Entrada_0(Q2), .Entrada_1(D2_pre), .Select_0(Liga), .Saida(D2));
  My_Mux_Down my_mux_down_7 (.Entrada_0(Q3), .Entrada_1(D3_pre), .Select_0(Liga), .Saida(D3));
  My_Mux_4bits my_mux_4bits_3 (
    .Entrada_0(4'b0000), .Entrada_1(my_mux_4bits_4_saida), .Select_0(Reset), .Saida({R4, R3, R2, R1}));
  My_Mux_4bits my_mux_4bits_4 (
    .Entrada_0(4'b1111), .Entrada_1(4'b1101), .Select_0(Cresce_Descresce), .Saida(my_mux_4bits_4_saida));
  My_Mux_Down my_mux_down_8 (.Entrada_0(Q4), .Entrada_1(D4_pre), .Select_0(Liga), .Saida(D4));

  // Other names for the same wires on the sheet: Cresce = Cresce_Descresce; Manual = Manual_Automatico

  // Notes on the sheet:
  //   CRESCENTE
  //   DESCRESCENTE
  //   ZERO = 0000
  //   DOIS = 1100
  //   Cresce = 0 => Crescente
  //   Cresce = 1 => Decrescente
  //   Se é ZERO ou DOIS
  //   CRESCENTE
  //   DESCRESCENTE
  //   Manual = 0 => CLOCK
  //   Manual = 1 => IMPULSO
  //   CRESCENTE
  //   DESCRESCENTE
  //   É crescente e NUM = 2 => CARRY
  //   É decrescente e NUM = 0 => Borrow
  //   CRESCENTE
  //   PINOS do SET
  //   DESCRESCENTE
  //   Se desligado, mantém o valor de Q, ou seja, não altera
  //   Se RESET + Crescente => volta pra ZERO
  //   Se RESET + Descrescente => volta pra DOIS
  //   PINOS do RESET
  //   Saídas
endmodule

module CountMOD5 (
  input  Cresce_Descresce,
  input  Reset,
  input  Impulso,
  input  Liga,
  input  Clock,
  input  Manual_Automatico,
  output Carry_Borrow,
  output Q1,
  output Q3,
  output Q2,
  output Q4
);

  wire and_1_out, and_2_out, and_3_out, and_4_out, and_5_out, and_6_out, and_7_out, and_8_out, and_9_out,
       and_10_out, and_11_out, D1, D1_pre, D2, D2_pre, D3, D3_pre, D4, D4_pre, Its_0, Its_4,
       my_mux_up_1_saida, not_1_out, not_2_out, not_3_out, not_4_out, not_5_out, not_6_out, not_7_out,
       not_8_out, not_9_out, not_10_out, or_1_out, or_2_out, or_4_out, R1, R2, R3, R4, S1, S2, S3, S4,
       xnor_1_out, xnor_2_out, xnor_3_out, xor_1_out, xor_2_out, xor_3_out;
  wire [3:0] my_mux_4bits_2_saida, my_mux_4bits_4_saida;

  not not_1 (not_1_out, Q1);
  and and_1 (and_1_out, not_1_out, not_2_out);
  not not_2 (not_2_out, Its_4);
  My_Mux_Down my_mux_down_1 (.Entrada_0(and_1_out), .Entrada_1(and_2_out), .Select_0(Cresce_Descresce), .Saida(D1_pre));
  not not_3 (not_3_out, Q1);
  not not_4 (not_4_out, Its_0);
  and and_2 (and_2_out, not_3_out, not_4_out);
  Num_00 num_00_1 (.in_1(Q1), .in_2(Q2), .in_3(Q3), .in_4(Q4), .out_5(Its_0));
  Num_04 num_04_1 (.in_1(Q1), .in_2(Q2), .in_3(Q3), .in_4(Q4), .out_5(Its_4));
  xor xor_1 (xor_1_out, Q1, Q2);
  not not_5 (not_5_out, Its_4);
  and and_3 (and_3_out, xor_1_out, not_5_out);
  My_Mux_Down my_mux_down_2 (.Entrada_0(and_3_out), .Entrada_1(and_4_out), .Select_0(Cresce_Descresce), .Saida(D2_pre));
  xnor xnor_1 (xnor_1_out, Q1, Q2);
  not not_6 (not_6_out, Its_0);
  and and_4 (and_4_out, xnor_1_out, not_6_out);
  D_Flip_Flop d_ff_1 (.D(D1), .clk(my_mux_up_1_saida), .Q(Q1), .preset(S1), .reset(R1));  // open: Qn
  Num_04 num_04_2 ();  // open: in_1, in_2, in_3, in_4, out_5
  D_Flip_Flop d_ff_2 (.D(D2), .clk(my_mux_up_1_saida), .Q(Q2), .preset(S2), .reset(R2));  // open: Qn
  and and_5 (and_5_out, Q1, Q2);
  xor xor_2 (xor_2_out, and_5_out, Q3);
  and and_6 (and_6_out, xor_2_out, not_7_out);
  My_Mux_Up my_mux_up_1 (
    .Entrada_0(Clock), .Entrada_1(Impulso), .Select_0(Manual_Automatico), .Saida(my_mux_up_1_saida));
  not not_7 (not_7_out, Its_4);
  D_Flip_Flop d_ff_3 (.D(D3), .clk(my_mux_up_1_saida), .Q(Q3), .preset(S3), .reset(R3));  // open: Qn
  not not_8 (not_8_out, Cresce_Descresce);
  and and_7 (and_7_out, not_8_out, Its_4);
  and and_8 (and_8_out, Cresce_Descresce, Its_0);
  My_Mux_Down my_mux_down_3 (.Entrada_0(and_6_out), .Entrada_1(or_2_out), .Select_0(Cresce_Descresce), .Saida(D3_pre));
  D_Flip_Flop d_ff_4 (.D(D4), .clk(my_mux_up_1_saida), .Q(Q4), .preset(S4), .reset(R4));  // open: Qn
  or or_1 (or_1_out, Q1, Q2);
  xnor xnor_2 (xnor_2_out, or_1_out, Q3);
  or or_2 (or_2_out, xnor_2_out, Its_0);
  or or_3 (Carry_Borrow, and_7_out, and_8_out);
  and and_9 (and_9_out, Q1, Q2, Q3);
  xor xor_3 (xor_3_out, and_9_out, Q4);
  not not_9 (not_9_out, Its_4);
  and and_10 (and_10_out, xor_3_out, not_9_out);
  My_Mux_Down my_mux_down_4 (.Entrada_0(Q1), .Entrada_1(D1_pre), .Select_0(Liga), .Saida(D1));
  My_Mux_4bits my_mux_4bits_1 (
    .Entrada_0(4'b0000), .Entrada_1(my_mux_4bits_2_saida), .Select_0(Reset), .Saida({S4, S3, S2, S1}));
  My_Mux_4bits my_mux_4bits_2 (
    .Entrada_0(4'b0000), .Entrada_1(4'b0100), .Select_0(Cresce_Descresce), .Saida(my_mux_4bits_2_saida));
  My_Mux_Down my_mux_down_5 (
    .Entrada_0(and_10_out), .Entrada_1(and_11_out), .Select_0(Cresce_Descresce), .Saida(D4_pre));
  or or_4 (or_4_out, Q1, Q2, Q3);
  xnor xnor_3 (xnor_3_out, or_4_out, Q4);
  not not_10 (not_10_out, Its_0);
  and and_11 (and_11_out, xnor_3_out, not_10_out);
  My_Mux_Down my_mux_down_6 (.Entrada_0(Q2), .Entrada_1(D2_pre), .Select_0(Liga), .Saida(D2));
  My_Mux_Down my_mux_down_7 (.Entrada_0(Q3), .Entrada_1(D3_pre), .Select_0(Liga), .Saida(D3));
  My_Mux_4bits my_mux_4bits_3 (
    .Entrada_0(4'b0000), .Entrada_1(my_mux_4bits_4_saida), .Select_0(Reset), .Saida({R4, R3, R2, R1}));
  My_Mux_4bits my_mux_4bits_4 (
    .Entrada_0(4'b1111), .Entrada_1(4'b1011), .Select_0(Cresce_Descresce), .Saida(my_mux_4bits_4_saida));
  My_Mux_Down my_mux_down_8 (.Entrada_0(Q4), .Entrada_1(D4_pre), .Select_0(Liga), .Saida(D4));

  // Other names for the same wires on the sheet: Cresce = Cresce_Descresce; Manual = Manual_Automatico

  // Notes on the sheet:
  //   CRESCENTE
  //   DESCRESCENTE
  //   ZERO = 0000
  //   QUATRO = 0010
  //   Cresce = 0 => Crescente
  //   Cresce = 1 => Decrescente
  //   Se é ZERO ou QUATRO
  //   CRESCENTE
  //   DESCRESCENTE
  //   Manual = 0 => CLOCK
  //   Manual = 1 => IMPULSO
  //   CRESCENTE
  //   DESCRESCENTE
  //   É crescente e NUM = QUATRO => CARRY
  //   É decrescente e NUM = 0 => Borrow
  //   CRESCENTE
  //   PINOS do SET
  //   DESCRESCENTE
  //   Se desligado, mantém o valor de Q, ou seja, não altera
  //   Se RESET + Crescente => volta pra ZERO
  //   Se RESET + Descrescente => volta pra DOIS
  //   PINOS do RESET
  //   Saídas
endmodule

module CountMOD6 (
  input  Cresce_Descresce,
  input  Reset,
  input  Impulso,
  input  Liga,
  input  Clock,
  input  Manual_Automatico,
  output Carry_Borrow,
  output Q1,
  output Q3,
  output Q2,
  output Q4
);

  wire and_1_out, and_2_out, and_3_out, and_4_out, and_5_out, and_6_out, and_7_out, and_8_out, and_9_out,
       and_10_out, D1, D1_pre, D2, D2_pre, D3, D3_pre, D4, D4_pre, Its_0, Its_5, my_mux_up_1_saida,
       not_1_out, not_2_out, not_3_out, not_4_out, not_5_out, not_6_out, not_7_out, not_8_out, not_9_out,
       or_1_out, or_2_out, or_3_out, or_5_out, R1, R2, R3, R4, S1, S2, S3, S4, xnor_1_out, xnor_2_out,
       xnor_3_out, xor_1_out, xor_2_out, xor_3_out;
  wire [3:0] my_mux_4bits_2_saida, my_mux_4bits_4_saida;

  not not_1 (not_1_out, Q1);
  and and_1 (and_1_out, not_1_out, not_2_out);
  not not_2 (not_2_out, Its_5);
  My_Mux_Down my_mux_down_1 (.Entrada_0(and_1_out), .Entrada_1(or_1_out), .Select_0(Cresce_Descresce), .Saida(D1_pre));
  not not_3 (not_3_out, Q1);
  or or_1 (or_1_out, not_3_out, Its_0);
  Num_00 num_00_1 (.in_1(Q1), .in_2(Q2), .in_3(Q3), .in_4(Q4), .out_5(Its_0));
  Num_05 num_05_1 (.in_1(Q1), .in_2(Q2), .in_3(Q3), .in_4(Q4), .out_5(Its_5));
  xor xor_1 (xor_1_out, Q1, Q2);
  not not_4 (not_4_out, Its_5);
  and and_2 (and_2_out, xor_1_out, not_4_out);
  My_Mux_Down my_mux_down_2 (.Entrada_0(and_2_out), .Entrada_1(and_3_out), .Select_0(Cresce_Descresce), .Saida(D2_pre));
  xnor xnor_1 (xnor_1_out, Q1, Q2);
  not not_5 (not_5_out, Its_0);
  and and_3 (and_3_out, xnor_1_out, not_5_out);
  D_Flip_Flop d_ff_1 (.D(D1), .clk(my_mux_up_1_saida), .Q(Q1), .preset(S1), .reset(R1));  // open: Qn
  D_Flip_Flop d_ff_2 (.D(D2), .clk(my_mux_up_1_saida), .Q(Q2), .preset(S2), .reset(R2));  // open: Qn
  and and_4 (and_4_out, Q1, Q2);
  xor xor_2 (xor_2_out, and_4_out, Q3);
  and and_5 (and_5_out, xor_2_out, not_6_out);
  My_Mux_Up my_mux_up_1 (
    .Entrada_0(Clock), .Entrada_1(Impulso), .Select_0(Manual_Automatico), .Saida(my_mux_up_1_saida));
  not not_6 (not_6_out, Its_5);
  D_Flip_Flop d_ff_3 (.D(D3), .clk(my_mux_up_1_saida), .Q(Q3), .preset(S3), .reset(R3));  // open: Qn
  not not_7 (not_7_out, Cresce_Descresce);
  and and_6 (and_6_out, not_7_out, Its_5);
  and and_7 (and_7_out, Cresce_Descresce, Its_0);
  My_Mux_Down my_mux_down_3 (.Entrada_0(and_5_out), .Entrada_1(or_3_out), .Select_0(Cresce_Descresce), .Saida(D3_pre));
  D_Flip_Flop d_ff_4 (.D(D4), .clk(my_mux_up_1_saida), .Q(Q4), .preset(S4), .reset(R4));  // open: Qn
  or or_2 (or_2_out, Q1, Q2);
  xnor xnor_2 (xnor_2_out, or_2_out, Q3);
  or or_3 (or_3_out, xnor_2_out, Its_0);
  or or_4 (Carry_Borrow, and_6_out, and_7_out);
  and and_8 (and_8_out, Q1, Q2, Q3);
  xor xor_3 (xor_3_out, and_8_out, Q4);
  not not_8 (not_8_out, Its_5);
  and and_9 (and_9_out, xor_3_out, not_8_out);
  My_Mux_Down my_mux_down_4 (.Entrada_0(Q1), .Entrada_1(D1_pre), .Select_0(Liga), .Saida(D1));
  My_Mux_4bits my_mux_4bits_1 (
    .Entrada_0(4'b0000), .Entrada_1(my_mux_4bits_2_saida), .Select_0(Reset), .Saida({S4, S3, S2, S1}));
  My_Mux_4bits my_mux_4bits_2 (
    .Entrada_0(4'b0000), .Entrada_1(4'b0101), .Select_0(Cresce_Descresce), .Saida(my_mux_4bits_2_saida));
  My_Mux_Down my_mux_down_5 (
    .Entrada_0(and_9_out), .Entrada_1(and_10_out), .Select_0(Cresce_Descresce), .Saida(D4_pre));
  or or_5 (or_5_out, Q1, Q2, Q3);
  xnor xnor_3 (xnor_3_out, or_5_out, Q4);
  not not_9 (not_9_out, Its_0);
  and and_10 (and_10_out, xnor_3_out, not_9_out);
  My_Mux_Down my_mux_down_6 (.Entrada_0(Q2), .Entrada_1(D2_pre), .Select_0(Liga), .Saida(D2));
  My_Mux_Down my_mux_down_7 (.Entrada_0(Q3), .Entrada_1(D3_pre), .Select_0(Liga), .Saida(D3));
  My_Mux_4bits my_mux_4bits_3 (
    .Entrada_0(4'b0000), .Entrada_1(my_mux_4bits_4_saida), .Select_0(Reset), .Saida({R4, R3, R2, R1}));
  My_Mux_4bits my_mux_4bits_4 (
    .Entrada_0(4'b1111), .Entrada_1(4'b1010), .Select_0(Cresce_Descresce), .Saida(my_mux_4bits_4_saida));
  My_Mux_Down my_mux_down_8 (.Entrada_0(Q4), .Entrada_1(D4_pre), .Select_0(Liga), .Saida(D4));

  // Other names for the same wires on the sheet: Cresce = Cresce_Descresce; Manual = Manual_Automatico

  // Notes on the sheet:
  //   CRESCENTE
  //   DESCRESCENTE
  //   ZERO = 0000
  //   CINCO = 1010
  //   Cresce = 0 => Crescente
  //   Cresce = 1 => Decrescente
  //   Se é ZERO ou CINCO
  //   CRESCENTE
  //   DESCRESCENTE
  //   Manual = 0 => CLOCK
  //   Manual = 1 => IMPULSO
  //   CRESCENTE
  //   DESCRESCENTE
  //   É crescente e NUM = 9 => CARRY
  //   É decrescente e NUM = 0 => Borrow
  //   CRESCENTE
  //   PINOS do SET
  //   DESCRESCENTE
  //   Se desligado, mantém o valor de Q, ou seja, não altera
  //   Se RESET + Crescente => volta pra ZERO
  //   Se RESET + Descrescente => volta pra NOVE
  //   PINOS do RESET
  //   Saídas
endmodule

module CountMOD10 (
  input  Cresce_Descrece,
  input  Reset,
  input  Impulso,
  input  Liga,
  input  Clock,
  input  Manual_Automatico,
  input  [3:0] Force_Num,
  output Carry_Borrow,
  output Q1,
  output Q3,
  output Q2,
  output Q4
);

  wire and_1_out, and_2_out, and_3_out, and_4_out, and_5_out, and_6_out, and_7_out, and_8_out, and_9_out,
       and_10_out, D1, D1_pre, D2, D2_pre, D3, D3_pre, D4, D4_pre, Its_0, Its_9, my_mux_up_1_saida,
       not_1_out, not_2_out, not_3_out, not_4_out, not_5_out, not_6_out, not_7_out, not_8_out, not_9_out,
       or_1_out, or_2_out, or_5_out, or_6_out, R1, R2, R3, R4, S1, S2, S3, S4, xnor_1_out, xnor_2_out,
       xnor_3_out, xor_1_out, xor_2_out, xor_3_out;
  wire [3:0] and_11_out, my_mux_4bits_1_saida, my_mux_4bits_2_saida, my_mux_4bits_3_saida,
       my_mux_4bits_4_saida, not_10_out;
  wire [3:3] or_8_out;

  not not_1 (not_1_out, Q1);
  and and_1 (and_1_out, not_1_out, not_2_out);
  not not_2 (not_2_out, Its_9);
  My_Mux_Down my_mux_down_1 (.Entrada_0(and_1_out), .Entrada_1(or_1_out), .Select_0(Cresce_Descrece), .Saida(D1_pre));
  not not_3 (not_3_out, Q1);
  or or_1 (or_1_out, not_3_out, Its_0);
  Num_00 num_00_1 (.in_1(Q1), .in_2(Q2), .in_3(Q3), .in_4(Q4), .out_5(Its_0));
  Num_09 num_09_1 (.in_1(Q1), .in_2(Q2), .in_3(Q3), .in_4(Q4), .out_5(Its_9));
  xor xor_1 (xor_1_out, Q1, Q2);
  not not_4 (not_4_out, Its_9);
  and and_2 (and_2_out, xor_1_out, not_4_out);
  My_Mux_Down my_mux_down_2 (.Entrada_0(and_2_out), .Entrada_1(and_3_out), .Select_0(Cresce_Descrece), .Saida(D2_pre));
  xnor xnor_1 (xnor_1_out, Q1, Q2);
  not not_5 (not_5_out, Its_0);
  and and_3 (and_3_out, xnor_1_out, not_5_out);
  D_Flip_Flop d_ff_1 (.D(D1), .clk(my_mux_up_1_saida), .Q(Q1), .preset(S1), .reset(R1));  // open: Qn
  D_Flip_Flop d_ff_2 (.D(D2), .clk(my_mux_up_1_saida), .Q(Q2), .preset(S2), .reset(R2));  // open: Qn
  and and_4 (and_4_out, Q1, Q2);
  xor xor_2 (xor_2_out, and_4_out, Q3);
  not not_6 (not_6_out, Its_9);
  and and_5 (and_5_out, xor_2_out, not_6_out);
  My_Mux_Up my_mux_up_1 (
    .Entrada_0(Clock), .Entrada_1(Impulso), .Select_0(Manual_Automatico), .Saida(my_mux_up_1_saida));
  D_Flip_Flop d_ff_3 (.D(D3), .clk(my_mux_up_1_saida), .Q(Q3), .preset(S3), .reset(R3));  // open: Qn
  not not_7 (not_7_out, Cresce_Descrece);
  and and_6 (and_6_out, not_7_out, Its_9);
  and and_7 (and_7_out, Cresce_Descrece, Its_0);
  or or_2 (or_2_out, Q1, Q2);
  My_Mux_Down my_mux_down_3 (.Entrada_0(and_5_out), .Entrada_1(and_8_out), .Select_0(Cresce_Descrece), .Saida(D3_pre));
  D_Flip_Flop d_ff_4 (.D(D4), .clk(my_mux_up_1_saida), .Q(Q4), .preset(S4), .reset(R4));  // open: Qn
  or or_3 (Carry_Borrow, and_6_out, and_7_out);
  xnor xnor_2 (xnor_2_out, or_2_out, Q3);
  not not_8 (not_8_out, Its_0);
  and and_8 (and_8_out, xnor_2_out, not_8_out);
  and and_9 (and_9_out, Q1, Q2, Q3);
  xor xor_3 (xor_3_out, and_9_out, Q4);
  not not_9 (not_9_out, Its_9);
  and and_10 (and_10_out, xor_3_out, not_9_out);
  My_Mux_Down my_mux_down_4 (.Entrada_0(and_10_out), .Entrada_1(or_6_out), .Select_0(Cresce_Descrece), .Saida(D4_pre));
  My_Mux_Down my_mux_down_5 (.Entrada_0(Q1), .Entrada_1(D1_pre), .Select_0(Liga), .Saida(D1));
  assign {S4, S3, S2, S1} = my_mux_4bits_1_saida | Force_Num;  // OR_Gate or_4, 4 bits wide
  My_Mux_4bits my_mux_4bits_1 (
    .Entrada_0(4'b0000), .Entrada_1(my_mux_4bits_2_saida), .Select_0(Reset), .Saida(my_mux_4bits_1_saida));
  My_Mux_4bits my_mux_4bits_2 (
    .Entrada_0(4'b0000), .Entrada_1(4'b1001), .Select_0(Cresce_Descrece), .Saida(my_mux_4bits_2_saida));
  or or_5 (or_5_out, Q1, Q2, Q3);
  My_Mux_Down my_mux_down_6 (.Entrada_0(Q2), .Entrada_1(D2_pre), .Select_0(Liga), .Saida(D2));
  xnor xnor_3 (xnor_3_out, or_5_out, Q4);
  or or_6 (or_6_out, xnor_3_out, Its_0);
  My_Mux_Down my_mux_down_7 (.Entrada_0(Q3), .Entrada_1(D3_pre), .Select_0(Liga), .Saida(D3));
  My_Mux_Down my_mux_down_8 (.Entrada_0(Q4), .Entrada_1(D4_pre), .Select_0(Liga), .Saida(D4));
  assign {R4, R3, R2, R1} = my_mux_4bits_3_saida | and_11_out;  // OR_Gate or_7, 4 bits wide
  My_Mux_4bits my_mux_4bits_3 (
    .Entrada_0(4'b0000), .Entrada_1(my_mux_4bits_4_saida), .Select_0(Reset), .Saida(my_mux_4bits_3_saida));
  My_Mux_4bits my_mux_4bits_4 (
    .Entrada_0(4'b1111), .Entrada_1(4'b0110), .Select_0(Cresce_Descrece), .Saida(my_mux_4bits_4_saida));
  assign and_11_out = {4{or_8_out[3]}} & not_10_out;  // AND_Gate and_11, 4 bits wide
  not not_10 (not_10_out[0], Force_Num[0]);
  not not_11 (not_10_out[1], Force_Num[1]);
  not not_12 (not_10_out[2], Force_Num[2]);
  not not_13 (not_10_out[3], Force_Num[3]);
  or or_8 (or_8_out[3], Force_Num[3], Force_Num[2], Force_Num[1], Force_Num[0]);

  // Other names for the same wires on the sheet: Cresce = Cresce_Descrece; ForceN[3:0] = Force_Num;
  //   Manual = Manual_Automatico

  // Notes on the sheet:
  //   CRESCENTE
  //   DESCRESCENTE
  //   ZERO = 0000
  //   NOVE = 1001
  //   Cresce = 0 => Crescente
  //   Cresce = 1 => Decrescente
  //   Manual = 0 => CLOCK
  //   Manual = 1 => Impulso
  //   Se é ZERO ou NOVE
  //   CRESCENTE
  //   DESCRESCENTE
  //   CRESCENTE
  //   DESCRESCENTE
  //   É crescente e NUM = 9 => CARRY
  //   É decrescente e NUM = 0 => Borrow
  //   CRESCENTE
  //   PINOS do SET
  //   DESCRESCENTE
  //   Se desligado, mantém o valor de Q, ou seja, não altera
  //   Se RESET + Crescente => volta pra ZERO
  //   Se RESET + Descrescente => volta pra NOVE
  //   PINOS do RESET
  //   Saídas
endmodule

module Count_9_OR_3 (
  input  Cresce_Descrece,
  input  Reset,
  input  Impulso,
  input  Liga,
  input  Clock,
  input  Manual_Automatico,
  input  Troca_Count,
  output Carry_Borrow,
  output Q1,
  output Q3,
  output Q2,
  output Q4
);

  wire and_1_out, and_2_out, and_3_out, and_4_out, and_5_out, and_6_out, and_7_out, and_8_out, and_9_out,
       and_10_out, and_11_out, and_12_out, and_13_out, and_14_out, and_15_out, and_16_out, and_17_out,
       and_18_out, and_19_out, and_20_out, D1, D1_pre, D2, D2_pre, D3, D3_pre, D4, D4_pre, Eh_Vinte, Its_0,
       Its_4, Its_9, my_mux_down_1_saida, my_mux_down_3_saida, my_mux_down_4_saida, my_mux_down_6_saida,
       my_mux_down_7_saida, my_mux_down_11_saida, my_mux_down_14_saida, my_mux_down_16_saida,
       my_mux_up_1_saida, not_1_out, not_2_out, not_3_out, not_4_out, not_5_out, not_6_out, not_7_out,
       not_8_out, not_9_out, not_10_out, not_11_out, not_12_out, not_13_out, not_14_out, not_15_out,
       not_16_out, not_17_out, not_18_out, not_19_out, not_20_out, or_1_out, or_3_out, or_4_out, or_5_out,
       or_6_out, or_7_out, or_8_out, R1, R2, R3, R4, S1, S2, S3, S4, xnor_1_out, xnor_2_out, xnor_3_out,
       xnor_4_out, xnor_5_out, xnor_6_out, xor_1_out, xor_2_out, xor_3_out, xor_4_out, xor_5_out, xor_6_out;
  wire [3:0] my_mux_4bits_2_saida, my_mux_4bits_4_saida;

  not not_1 (not_1_out, Q1);
  not not_2 (not_2_out, Its_9);
  and and_1 (and_1_out, not_1_out, not_2_out);
  not not_3 (not_3_out, Q1);
  My_Mux_Down my_mux_down_1 (
    .Entrada_0(and_1_out), .Entrada_1(and_2_out), .Select_0(Troca_Count), .Saida(my_mux_down_1_saida));
  not not_4 (not_4_out, Its_4);
  and and_2 (and_2_out, not_3_out, not_4_out);
  My_Mux_Down my_mux_down_2 (
    .Entrada_0(my_mux_down_1_saida), .Entrada_1(my_mux_down_3_saida), .Select_0(Cresce_Descrece),
    .Saida(D1_pre));
  not not_5 (not_5_out, Q1);
  or or_1 (or_1_out, not_5_out, Its_0);
  My_Mux_Down my_mux_down_3 (
    .Entrada_0(or_1_out), .Entrada_1(and_3_out), .Select_0(Troca_Count), .Saida(my_mux_down_3_saida));
  not not_6 (not_6_out, Q1);
  not not_7 (not_7_out, Its_0);
  and and_3 (and_3_out, not_6_out, not_7_out);
  Num_00 num_00_1 (.in_1(Q1), .in_2(Q2), .in_3(Q3), .in_4(Q4), .out_5(Its_0));
  Num_09 num_09_1 (.in_1(Q1), .in_2(Q2), .in_3(Q3), .in_4(Q4), .out_5(Its_9));
  Num_04 num_04_1 (.in_1(Q1), .in_2(Q2), .in_3(Q3), .in_4(Q4), .out_5(Its_4));
  xor xor_1 (xor_1_out, Q1, Q2);
  and and_4 (and_4_out, xor_1_out, not_8_out);
  not not_8 (not_8_out, Its_9);
  My_Mux_Down my_mux_down_4 (
    .Entrada_0(and_4_out), .Entrada_1(and_5_out), .Select_0(Troca_Count), .Saida(my_mux_down_4_saida));
  D_Flip_Flop d_ff_1 (.D(D1), .clk(my_mux_up_1_saida), .Q(Q1), .preset(S1), .reset(R1));  // open: Qn
  xor xor_2 (xor_2_out, Q1, Q2);
  not not_9 (not_9_out, Its_4);
  and and_5 (and_5_out, xor_2_out, not_9_out);
  D_Flip_Flop d_ff_2 (.D(D2), .clk(my_mux_up_1_saida), .Q(Q2), .preset(S2), .reset(R2));  // open: Qn
  xnor xnor_1 (xnor_1_out, Q1, Q2);
  My_Mux_Down my_mux_down_5 (
    .Entrada_0(my_mux_down_4_saida), .Entrada_1(my_mux_down_6_saida), .Select_0(Cresce_Descrece),
    .Saida(D2_pre));
  My_Mux_Up my_mux_up_1 (
    .Entrada_0(Clock), .Entrada_1(Impulso), .Select_0(Manual_Automatico), .Saida(my_mux_up_1_saida));
  not not_10 (not_10_out, Its_0);
  and and_6 (and_6_out, xnor_1_out, not_10_out);
  My_Mux_Down my_mux_down_6 (
    .Entrada_0(and_6_out), .Entrada_1(and_10_out), .Select_0(Troca_Count), .Saida(my_mux_down_6_saida));
  D_Flip_Flop d_ff_3 (.D(D3), .clk(my_mux_up_1_saida), .Q(Q3), .preset(S3), .reset(R3));  // open: Qn
  not not_11 (not_11_out, Cresce_Descrece);
  not not_12 (not_12_out, Eh_Vinte);
  and and_7 (and_7_out, not_11_out, not_12_out, Its_9);
  not not_13 (not_13_out, Cresce_Descrece);
  and and_8 (and_8_out, not_13_out, Eh_Vinte, Its_4);
  and and_9 (and_9_out, Cresce_Descrece, Its_0);
  xnor xnor_2 (xnor_2_out, Q1, Q2);
  and and_10 (and_10_out, xnor_2_out, not_14_out);
  D_Flip_Flop d_ff_4 (.D(D4), .clk(my_mux_up_1_saida), .Q(Q4), .preset(S4), .reset(R4));  // open: Qn
  not not_14 (not_14_out, Its_0);
  or or_2 (Carry_Borrow, and_7_out, and_8_out, and_9_out);
  and and_11 (and_11_out, Q1, Q2);
  xor xor_3 (xor_3_out, and_11_out, Q3);
  and and_12 (and_12_out, xor_3_out, not_15_out);
  not not_15 (not_15_out, Its_9);
  My_Mux_Down my_mux_down_7 (
    .Entrada_0(and_12_out), .Entrada_1(and_14_out), .Select_0(Troca_Count), .Saida(my_mux_down_7_saida));
  and and_13 (and_13_out, Q1, Q2);
  xor xor_4 (xor_4_out, and_13_out, Q3);
  not not_16 (not_16_out, Its_4);
  and and_14 (and_14_out, xor_4_out, not_16_out);
  My_Mux_Down my_mux_down_8 (
    .Entrada_0(my_mux_down_7_saida), .Entrada_1(my_mux_down_11_saida), .Select_0(Cresce_Descrece),
    .Saida(D3_pre));
  My_Mux_Down my_mux_down_9 (.Entrada_0(Q1), .Entrada_1(D1_pre), .Select_0(Liga), .Saida(D1));
  My_Mux_4bits my_mux_4bits_1 (
    .Entrada_0(4'b0000), .Entrada_1(my_mux_4bits_2_saida), .Select_0(Reset), .Saida({S4, S3, S2, S1}));
  My_Mux_4bits my_mux_4bits_2 (
    .Entrada_0(4'b0000), .Entrada_1(4'b0100), .Select_0(Cresce_Descrece), .Saida(my_mux_4bits_2_saida));
  or or_3 (or_3_out, Q1, Q2);
  xnor xnor_3 (xnor_3_out, or_3_out, Q3);
  and and_15 (and_15_out, xnor_3_out, not_17_out);
  My_Mux_Down my_mux_down_10 (.Entrada_0(Q2), .Entrada_1(D2_pre), .Select_0(Liga), .Saida(D2));
  not not_17 (not_17_out, Its_0);
  My_Mux_Down my_mux_down_11 (
    .Entrada_0(and_15_out), .Entrada_1(or_5_out), .Select_0(Troca_Count), .Saida(my_mux_down_11_saida));
  or or_4 (or_4_out, Q1, Q2);
  xnor xnor_4 (xnor_4_out, or_4_out, Q3);
  or or_5 (or_5_out, xnor_4_out, Its_0);
  My_Mux_Down my_mux_down_12 (.Entrada_0(Q3), .Entrada_1(D3_pre), .Select_0(Liga), .Saida(D3));
  My_Mux_4bits my_mux_4bits_3 (
    .Entrada_0(4'b0000), .Entrada_1(my_mux_4bits_4_saida), .Select_0(Reset), .Saida({R4, R3, R2, R1}));
  My_Mux_4bits my_mux_4bits_4 (
    .Entrada_0(4'b1111), .Entrada_1(4'b1011), .Select_0(Cresce_Descrece), .Saida(my_mux_4bits_4_saida));
  My_Mux_Down my_mux_down_13 (.Entrada_0(Q4), .Entrada_1(D4_pre), .Select_0(Liga), .Saida(D4));
  and and_16 (and_16_out, Q1, Q2, Q3);
  xor xor_5 (xor_5_out, and_16_out, Q4);
  not not_18 (not_18_out, Its_9);
  and and_17 (and_17_out, xor_5_out, not_18_out);
  My_Mux_Down my_mux_down_14 (
    .Entrada_0(and_17_out), .Entrada_1(and_19_out), .Select_0(Troca_Count), .Saida(my_mux_down_14_saida));
  and and_18 (and_18_out, Q1, Q2, Q3);
  xor xor_6 (xor_6_out, and_18_out, Q4);
  not not_19 (not_19_out, Its_4);
  and and_19 (and_19_out, xor_6_out, not_19_out);
  or or_6 (or_6_out, Q1, Q2, Q3);
  xnor xnor_5 (xnor_5_out, or_6_out, Q4);
  My_Mux_Down my_mux_down_15 (
    .Entrada_0(my_mux_down_14_saida), .Entrada_1(my_mux_down_16_saida), .Select_0(Cresce_Descrece),
    .Saida(D4_pre));
  or or_7 (or_7_out, xnor_5_out, Its_0);
  My_Mux_Down my_mux_down_16 (
    .Entrada_0(or_7_out), .Entrada_1(and_20_out), .Select_0(Troca_Count), .Saida(my_mux_down_16_saida));
  or or_8 (or_8_out, Q1, Q2, Q3);
  xnor xnor_6 (xnor_6_out, or_8_out, Q4);
  and and_20 (and_20_out, xnor_6_out, not_20_out);
  not not_20 (not_20_out, Its_0);

  // Other names for the same wires on the sheet: Cresce = Cresce_Descrece; Manual = Manual_Automatico;
  //   Troca = Troca_Count

  // Notes on the sheet:
  //   0-9
  //   0-4
  //   CRESCENTE
  //   0-9
  //   DESCRESCENTE
  //   0-4
  //   Cresce = 0 => Crescente
  //   Cresce = 1 => Decrescente
  //   Manual = 0 => CLOCK
  //   Manual = 1 => Impulso
  //   0-9
  //   0-4
  //   CRESCENTE
  //   0-9
  //   DESCRESCENTE
  //   0-4
  //   0-9
  //   É crescente, dezena é 20 e NUM = 4 => CARRY
  //   É decrescente e NUM = 0 => Borrow
  //   É crescente, dezena não é 20 e NUM = 9 => CARRY
  //   0-4
  //   CRESCENTE
  //   PINOS do SET
  //   0-9
  //   DESCRESCENTE
  //   Se desligado, mantém o valor de Q, ou seja, não altera
  //   Se RESET + Crescente => volta pra ZERO
  //   Se RESET + Descrescente => volta pra NOVE
  //   0-4
  //   PINOS do RESET
  //   0-9
  //   Saídas
  //   0-4
  //   CRESCENTE
  //   0-9
  //   DESCRESCENTE
  //   0-4
endmodule

module Alavanca (
  input  in_1,
  output out_2
);

  wire d_ff_1_qn;

  D_Flip_Flop d_ff_1 (.D(d_ff_1_qn), .clk(in_1), .Q(out_2), .Qn(d_ff_1_qn));  // open: preset, reset
endmodule

module Num_00 (
  input  in_1,
  input  in_2,
  input  in_3,
  input  in_4,
  output out_5
);

  wire not_1_out, not_2_out, not_3_out, not_4_out;

  not not_1 (not_1_out, in_1);
  not not_2 (not_2_out, in_2);
  not not_3 (not_3_out, in_3);
  not not_4 (not_4_out, in_4);
  and and_1 (out_5, not_1_out, not_2_out, not_3_out, not_4_out);
endmodule

module Num_02 (
  input  in_1,
  input  in_2,
  input  in_3,
  input  in_4,
  output out_5
);

  wire not_1_out, not_2_out, not_3_out;

  not not_1 (not_1_out, in_1);
  not not_2 (not_2_out, in_3);
  not not_3 (not_3_out, in_4);
  and and_1 (out_5, not_1_out, in_2, not_2_out, not_3_out);
endmodule

module Num_03 (
  input  in_1,
  input  in_2,
  input  in_3,
  input  in_4,
  output out_5
);

  wire not_1_out, not_2_out;

  not not_1 (not_1_out, in_3);
  not not_2 (not_2_out, in_4);
  and and_1 (out_5, in_1, in_2, not_1_out, not_2_out);
endmodule

module Num_04 (
  input  in_1,
  input  in_2,
  input  in_3,
  input  in_4,
  output out_5
);

  wire not_1_out, not_2_out, not_3_out;

  not not_1 (not_1_out, in_1);
  not not_2 (not_2_out, in_2);
  not not_3 (not_3_out, in_4);
  and and_1 (out_5, not_1_out, not_2_out, in_3, not_3_out);
endmodule

module Num_05 (
  input  in_1,
  input  in_2,
  input  in_3,
  input  in_4,
  output out_5
);

  wire not_1_out, not_2_out;

  not not_1 (not_1_out, in_2);
  not not_2 (not_2_out, in_4);
  and and_1 (out_5, in_1, not_1_out, in_3, not_2_out);
endmodule

module Num_09 (
  input  in_1,
  input  in_2,
  input  in_3,
  input  in_4,
  output out_5
);

  wire not_1_out, not_2_out;

  not not_1 (not_1_out, in_2);
  not not_2 (not_2_out, in_3);
  and and_1 (out_5, in_1, not_1_out, not_2_out, in_4);
endmodule

module My_Mux_Up (
  input  Entrada_0,
  input  Entrada_1,
  input  Select_0,
  output Saida
);

  wire and_1_out, and_2_out, not_1_out;

  not not_1 (not_1_out, Select_0);
  and and_1 (and_1_out, Entrada_0, not_1_out);
  and and_2 (and_2_out, Entrada_1, Select_0);
  or or_1 (Saida, and_1_out, and_2_out);
endmodule

module My_Mux_Down (
  input  Entrada_0,
  input  Entrada_1,
  input  Select_0,
  output Saida
);

  wire and_1_out, and_2_out, not_1_out;

  not not_1 (not_1_out, Select_0);
  and and_1 (and_1_out, Entrada_0, not_1_out);
  and and_2 (and_2_out, Entrada_1, Select_0);
  or or_1 (Saida, and_1_out, and_2_out);
endmodule

module My_Mux_4bits (
  input  [3:0] Entrada_0,
  input  [3:0] Entrada_1,
  input  Select_0,
  output [3:0] Saida
);

  wire [3:0] and_1_out, and_2_out, not_1_out;

  assign not_1_out = ~{4{Select_0}};  // NOT_Gate not_1, 4 bits wide
  assign and_1_out = Entrada_0 & not_1_out;  // AND_Gate and_1, 4 bits wide
  assign and_2_out = Entrada_1 & {4{Select_0}};  // AND_Gate and_2, 4 bits wide
  assign Saida = and_1_out | and_2_out;  // OR_Gate or_1, 4 bits wide
endmodule
